// Logisim project finalmilestone.circ as structural Verilog: 2 circuits, main circuit main
// T6
module main (
  input  INC_AR,
  input  CLR_AR,
  input  CLR_PC,
  input  INC_AC,
  input  CLR_AC,
  input  CLR_DR,
  input  LD_TR,
  input  INC_TR,
  input  CLR_TR,
  input  in_10,
  input  [15:0] in_11
);

  wire A4, A5, A6, A7, A8, A9, A10, A11, AC_LD, ADD, ADD_SIG, ALL_OPS, ALU_OPS, BUN, C0, C1, C2, CLOCK_out,
       CLR_SC, d_ff_1_q, DIV, DIV_SIG, DR_LD, DR_ZERO, INC_DR, INC_PC, ISZ, LD_AR, LDA, LDA_SIG, MEMOPS,
       OP12, OP13, OP14, OP15, read, S0, S1, S2, STA, T0, T1, T2, T3, T3BUN, T3STA, T4, T4_OPS, T5, T5ISZ,
       T6, T6ISZ, write, XOR, XOR_SIG, ZERO;
  wire [2:0] SC_q;
  wire [3:0] IR_q;
  wire [7:0] AR_q, bit_extender_1_out, bit_extender_2_out, PC_q;
  wire [15:0] AC_q, ALU_output, bit_extender_3_out, bit_extender_4_out, bit_extender_5_out, DR_q,
       multiplexer_1_out, ram_1_data, TR_q;

  Clock CLOCK (.out(CLOCK_out));
  Counter #(.width(3), .max('h6)) SC (
    .load(in_10), .count(1'b1), .Q(SC_q), .clk(CLOCK_out), .clr(d_ff_1_q));  // open: D, carry
  Bit_Extender #(.in_width(16), .out_width(8)) bit_extender_1 (.in(multiplexer_1_out), .out(bit_extender_1_out));
  Bit_Extender #(.in_width(16), .out_width(8)) bit_extender_2 (.in(multiplexer_1_out), .out(bit_extender_2_out));
  ALU ALU (.DR(DR_q), .AC(AC_q), .C2C1C0({C2, C1, C0}), .OUTPUT(ALU_output));
  D_Flip_Flop d_ff_1 (.clk(CLOCK_out), .D(CLR_SC), .Q(d_ff_1_q));  // open: Qn, preset, en, reset
  Counter AR (
    .load(LD_AR), .D(bit_extender_1_out), .count(INC_AR), .Q(AR_q), .clk(CLOCK_out), .clr(CLR_AR));  // open: carry
  Counter PC (
    .load(T3BUN), .D(bit_extender_2_out), .count(INC_PC), .Q(PC_q), .clk(CLOCK_out), .clr(CLR_PC));  // open: carry
  Counter #(.width(16), .max('hffff)) DR (
    .load(DR_LD), .D(multiplexer_1_out), .count(INC_DR), .Q(DR_q), .clk(CLOCK_out), .clr(CLR_DR));  // open: carry
  Counter #(.width(16), .max('hffff)) TR (
    .load(LD_TR), .D(multiplexer_1_out), .count(INC_TR), .Q(TR_q), .clk(CLOCK_out), .clr(CLR_TR));  // open: carry
  Register #(.width(16)) IR (
    .D(multiplexer_1_out), .en(T1), .Q({OP15, OP14, OP13, OP12, A11, A10, A9, A8, A7, A6, A5, A4, IR_q}),
    .clk(CLOCK_out));  // open: clr
  Decoder #(.select(3), .enable("false")) decoder_1 (
    .out0(T0), .out1(T1), .out2(T2), .out3(T3), .out4(T4), .out5(T5), .out6(T6), .sel(SC_q));  // open: out7
  assign bit_extender_3_out = {{8{1'b0}}, AR_q};  // Bit_Extender bit_extender_3
  assign bit_extender_4_out = {{8{1'b0}}, PC_q};  // Bit_Extender bit_extender_4
  Counter #(.width(16), .max('hffff)) AC (
    .load(AC_LD), .D(ALU_output), .count(INC_AC), .Q(AC_q), .clk(CLOCK_out), .clr(CLR_AC));  // open: carry
  RAM #(.dataWidth(16), .bus("separate")) ram_1 (
    .addr(AR_q), .din(multiplexer_1_out), .data(ram_1_data), .str(write), .sel(1'b1), .clk(CLOCK_out),
    .ld(read));  // open: clr
  assign bit_extender_5_out = {{8{1'b0}}, {A11, A10, A9, A8, A7, A6, A5, A4}};  // Bit_Extender bit_extender_5
  Comparator #(.width(16)) comparator_1 (.a(DR_q), .b(in_11), .eq(DR_ZERO));  // open: gt, lt
  Multiplexer #(.select(3), .width(16), .enable("false")) multiplexer_1 (
    .in1(bit_extender_3_out), .in2(bit_extender_4_out), .in3(AC_q), .in4(DR_q), .in5(TR_q), .in6(ram_1_data),
    .in7(bit_extender_5_out), .out(multiplexer_1_out), .sel({S2, S1, S0}));  // open: in0
  and and_1 (DIV_SIG, DIV, T4);
  or or_1 (C2, DIV_SIG, XOR_SIG);
  or or_2 (C1, XOR_SIG, ADD_SIG);
  or or_3 (C0, LDA_SIG, DIV_SIG, XOR_SIG);
  and and_2 (ZERO, T6, ISZ, DR_ZERO);
  or or_4 (INC_PC, T1, ZERO);
  Decoder #(.select(4), .disabled(0), .enable("false")) decoder_2 (
    .out0(XOR), .out1(ADD), .out2(LDA), .out3(STA), .out4(BUN), .out5(DIV), .out6(ISZ),
    .sel({OP15, OP14, OP13, OP12}));  // open: out7, out8, out9, out10, out11, out12, out13, out14, out15
  and and_3 (XOR_SIG, T4, XOR);
  and and_4 (ADD_SIG, ADD, T4);
  and and_5 (T5ISZ, T5, ISZ);
  and and_6 (T3STA, T3, STA);
  and and_7 (T6ISZ, T6, ISZ);
  and and_8 (INC_DR, ISZ, T4);
  and and_9 (LDA_SIG, T4, LDA);
  or or_5 (S0, T3STA, T2);
  or or_6 (S1, T0, T1, T2, T3STA, DR_LD);
  or or_7 (S2, T1, T2, DR_LD, T5ISZ);
  or or_8 (ALU_OPS, LDA, ADD, XOR, DIV);
  or or_9 (write, T3STA, T5ISZ);
  or or_10 (CLR_SC, T4_OPS, T6ISZ);
  and and_10 (AC_LD, ALU_OPS, T4);
  or or_11 (read, T1, DR_LD);
  or or_12 (MEMOPS, LDA, ADD, XOR, DIV, ISZ);
  or or_13 (ALL_OPS, LDA, ADD, XOR, DIV, BUN, STA);
  or or_14 (LD_AR, T0, T2);
  and and_11 (DR_LD, T3, MEMOPS);
  and and_12 (T4_OPS, T4, ALL_OPS);
  and and_13 (T3BUN, T3, BUN);

  // Other names for the same wires on the sheet: T3MEMOPS = DR_LD
endmodule

module ALU (
  input  [15:0] DR,
  input  [15:0] AC,
  input  [2:0] C2C1C0,
  output [15:0] OUTPUT
);

  wire [15:0] adder_1_out, divider_1_out, multiplier_1_out, not_1_out, subtractor_1_out, xor_1_out;

  Adder #(.width(16)) adder_1 (.a(DR), .b(AC), .out(adder_1_out));  // open: cin, cout
  Subtractor #(.width(16)) subtractor_1 (.a(DR), .b(AC), .out(subtractor_1_out));  // open: bin, bout
  Multiplier #(.width(16)) multiplier_1 (.a(DR), .b(AC), .out(multiplier_1_out));  // open: cin, cout
  Divider #(.width(16)) divider_1 (.a(AC), .b(DR), .out(divider_1_out));  // open: upper, rem
  assign not_1_out = ~DR;  // NOT_Gate not_1, 16 bits wide
  assign xor_1_out = DR ^ AC;  // XOR_Gate xor_1, 16 bits wide
  Multiplexer #(.select(3), .width(16), .enable("false")) multiplexer_1 (
    .in1(DR), .in2(adder_1_out), .in3(subtractor_1_out), .in4(multiplier_1_out), .in5(divider_1_out),
    .in6(not_1_out), .in7(xor_1_out), .out(OUTPUT), .sel(C2C1C0));  // open: in0
endmodule
